# Fritzing sketch cansat (saved by Fritzing 0.9.3b)
circuit board: 8.67471cm x 5.86848cm
breadboards: 1

parts:
  Componente1 = Arduino Nano (Rev3.0)
  Componente2 = Barometric Pressure Sensor - BMP180 Breakout (GY-68)
  Componente3 = InvenSense MPU6050
  VCC1 = Battery
  microSD1 = MicroSD Card Module

nets (from the schematic view):
  GND: Componente1.GND, Componente2.GND, Componente3.GND, VCC1.-, microSD1.GND
  N1: Componente1.D2, Componente3.INT
  N2: Componente1.D4, microSD1.CS
  N3: Componente1.D11/MOSI, microSD1.MOSI
  N4: Componente1.D12/MISO, microSD1.MISO
  5V: Componente1.5V, Componente2.VCC, VCC1.+
  N5: Componente1.A5, Componente2.SCL, Componente3.SCL
  N6: Componente1.A4, Componente2.SDA, Componente3.SDA
  N7: Componente1.D13/SCK, microSD1.SCK
  VCC: Componente3.VCC, microSD1.VCC
